# Fritzing sketch bluetooth_ rename_ (saved by Fritzing 0.9.3b)

parts:
  Part1 = Bluetooth HC-05 Macho
  Part2 = Arduino Uno (Rev3) - ICSP

nets:
  N1: Part1.TXD, Part2.D1/TX
  N2: Part1.RXD, Part2.D0/RX
  VCC: Part1.VCC, Part2.5V
  N3: Part1.Key, Part2.RESET
  GND: Part1.GND, Part2.GND
